// Digital circuit lab10final.dig as structural Verilog
module lab10final (
  input  [8:0] N,
  input  reset,
  input  start,
  input  clock,
  output [7:0] displayout,
  output valid,
  output done,
  output [15:0] clockcount
);

  wire _3to0, and_2_out, and_3_out, and_4_out, and_5_out, and_6_out, and_7_out, clrovf, clrovf2,
       comparator_1_eq, comparator_1_lt, comparator_2_eq, comparator_2_lt, d_ff_1_q, d_ff_2_nq, d_ff_3_q,
       d_ff_5_q, d_ff_6_q, dataset, finish, multiplexer_1_out, multiplexer_3_out, multiplexer_4_out,
       multiplexer_5_out, multiplexer_6_out, multiplexer_7_out, multiplexer_12_out, multiplexer_13_out,
       multiplexer_15_out, next, not_1_out, or_4_out, ovf, reset_t, start_t;
  wire [0:0] paddress;
  wire [1:0] d_ff_4_q, state;
  wire [7:0] add_2_s, d_ff_8_q, multiplexer_8_out, multiplexer_11_out, multiplexer_14_out, ramout, romval;
  wire [8:0] add_1_s, counter_1_out, counter_3_out, counter_5_out, multiplexer_2_out, multiplexer_9_out;
  wire [8:1] counter_4_out;

  not not_1 (not_1_out, ovf);
  Multiplexer #(.Selector_Bits(2)) multiplexer_1 (
    .sel(state), .in_0(1'b0), .in_1(1'b0), .in_2(not_1_out), .in_3(1'b0), .out(multiplexer_1_out));
  or or_1 (reset_t, _3to0, reset);
  D_FF d_ff_1 (.D(start), .C(clock), .Q(d_ff_1_q));  // open: nQ
  Counter #(.Bits(9)) counter_1 (.en(multiplexer_1_out), .C(clock), .clr(reset_t), .out(counter_1_out));  // open: ovf
  D_FF d_ff_2 (.D(d_ff_1_q), .C(clock), .nQ(d_ff_2_nq));  // open: Q
  D_FF d_ff_3 (.D(start), .C(clock), .Q(d_ff_3_q));  // open: nQ
  and and_1 (start_t, d_ff_2_nq, d_ff_3_q);
  Comparator #(.Bits(9)) comparator_1 (
    .a(N), .b(counter_1_out), .eq(comparator_1_eq), .lt(comparator_1_lt));  // open: gt
  Multiplexer #(.Selector_Bits(2), .Bits(9)) multiplexer_2 (
    .sel(state), .in_0({9{1'b0}}), .in_1({9{1'b0}}), .in_2(counter_1_out), .in_3({9{1'b0}}),
    .out(multiplexer_2_out));
  Multiplexer #(.Selector_Bits(2)) multiplexer_3 (
    .sel(state), .in_0(1'b0), .in_1(1'b0), .in_2(1'b1), .in_3(1'b0), .out(multiplexer_3_out));
  or or_2 (finish, comparator_1_eq, comparator_1_lt);
  ROM #(.AddrBits(9), .isProgramMemory("true"), .Bits(8)) ROMFILE (
    .A(multiplexer_2_out), .sel(multiplexer_3_out), .D(romval));
  Multiplexer #(.Selector_Bits(2)) multiplexer_4 (
    .sel(state), .in_0(start_t), .in_1(1'b1), .in_2(finish), .in_3(clrovf2), .out(multiplexer_4_out));
  Counter #(.Bits(2)) counter_2 (.en(multiplexer_4_out), .C(clock), .clr(reset_t), .out(state));  // open: ovf
  Multiplexer #(.Selector_Bits(2)) multiplexer_5 (
    .sel(state), .in_0(1'b0), .in_1(1'b0), .in_2(1'b0), .in_3(1'b1), .out(multiplexer_5_out));
  D_FF #(.Bits(2)) d_ff_4 (.D(state), .C(clock), .Q(d_ff_4_q));  // open: nQ
  and and_2 (and_2_out, ~next, dataset);  // And
  and and_3 (and_3_out, d_ff_4_q[0], d_ff_4_q[1], ~state[0], ~state[1]);  // And
  Multiplexer #(.Selector_Bits(2)) multiplexer_6 (
    .sel(state), .in_0(1'b0), .in_1(1'b1), .in_2(1'b0), .in_3(1'b0), .out(multiplexer_6_out));
  D_FF d_ff_5 (.D(ovf), .C(clock), .Q(d_ff_5_q));  // open: nQ
  Multiplexer multiplexer_7 (.sel(and_2_out), .in_0(multiplexer_5_out), .in_1(1'b0), .out(multiplexer_7_out));
  or or_3 (_3to0, done, and_3_out);
  Counter #(.Bits(9)) counter_3 (.en(multiplexer_6_out), .C(clock), .clr(reset_t), .out(counter_3_out), .ovf(clrovf));
  Add #(.Bits(9)) add_1 (.a({romval, 1'b0}), .b({9{1'b0}}), .c_i(d_ff_5_q), .s(add_1_s));  // open: c_o
  Counter #(.Bits(9)) counter_4 (
    .en(multiplexer_7_out), .C(clock), .clr(reset_t), .out({counter_4_out, dataset}), .ovf(clrovf2));
  and and_4 (and_4_out, clock, ~dataset);  // And
  Add #(.Bits(8)) add_2 (.a(ramout), .b({8{1'b0}}), .c_i(1'b1), .s(add_2_s), .c_o(ovf));
  Multiplexer #(.Bits(8)) multiplexer_8 (.sel(finish), .in_0(add_2_s), .in_1(ramout), .out(multiplexer_8_out));
  D_FF d_ff_6 (.D(_3to0), .C(clock), .Q(d_ff_6_q));  // open: nQ
  Multiplexer #(.Selector_Bits(2), .Bits(9)) multiplexer_9 (
    .sel(state), .in_0({9{1'b0}}), .in_1(counter_3_out), .in_2(add_1_s), .in_3({counter_4_out, dataset}),
    .out(multiplexer_9_out));
  D_FF #(.Bits(9)) d_ff_7 (.D({counter_4_out, dataset}), .C(and_4_out), .Q({displayout, paddress[0]}));  // open: nQ
  Multiplexer multiplexer_10 (.sel(start_t), .in_0(d_ff_6_q), .in_1(1'b0), .out(done));
  Multiplexer #(.Selector_Bits(2), .Bits(8)) multiplexer_11 (
    .sel(state), .in_0({8{1'b0}}), .in_1({8{1'b0}}), .in_2(multiplexer_8_out), .in_3({8{1'b0}}),
    .out(multiplexer_11_out));
  Multiplexer #(.Selector_Bits(2)) multiplexer_12 (
    .sel(state), .in_0(1'b0), .in_1(1'b1), .in_2(1'b1), .in_3(1'b0), .out(multiplexer_12_out));
  Multiplexer #(.Selector_Bits(2)) multiplexer_13 (
    .sel(state), .in_0(1'b0), .in_1(1'b1), .in_2(1'b1), .in_3(1'b1), .out(multiplexer_13_out));
  RAMDualPort #(.AddrBits(9), .Bits(8)) RAM (
    .A(multiplexer_9_out), .Din(multiplexer_11_out), .str(multiplexer_12_out), .C(clock),
    .ld(multiplexer_13_out), .D(ramout));
  Seven_Seg_Hex seven_seg_hex_1 (.d(displayout[7:4]), .dp(1'b0));
  and and_5 (and_5_out, clock, ~dataset);  // And
  Seven_Seg_Hex seven_seg_hex_2 (.d(displayout[3:0]), .dp(1'b0));
  Multiplexer #(.Selector_Bits(2), .Bits(8)) multiplexer_14 (
    .sel(state), .in_0({8{1'b0}}), .in_1({8{1'b0}}), .in_2({8{1'b0}}), .in_3(ramout), .out(multiplexer_14_out));
  and and_6 (and_6_out, ~next, dataset);  // And
  or or_4 (or_4_out, reset_t, next);
  and and_7 (and_7_out, ~next, dataset);  // And
  Multiplexer #(.Selector_Bits(2)) multiplexer_15 (
    .sel(state), .in_0(1'b0), .in_1(1'b1), .in_2(1'b1), .in_3(1'b1), .out(multiplexer_15_out));
  D_FF #(.Bits(8)) d_ff_8 (.D(multiplexer_14_out), .C(and_5_out), .Q(d_ff_8_q));  // open: nQ
  Counter #(.Bits(9)) counter_5 (.en(and_6_out), .C(clock), .clr(or_4_out), .out(counter_5_out));  // open: ovf
  Multiplexer #(.Selector_Bits(2)) multiplexer_16 (
    .sel(state), .in_0(1'b0), .in_1(1'b0), .in_2(1'b0), .in_3(and_7_out), .out(valid));
  Counter #(.Bits(16)) counter_6 (.en(multiplexer_15_out), .C(clock), .clr(start_t), .out(clockcount));  // open: ovf
  Comparator #(.Bits(9)) comparator_2 (
    .a({multiplexer_14_out[0], d_ff_8_q}), .b(counter_5_out), .eq(comparator_2_eq), .lt(comparator_2_lt));  // open: gt
  or or_5 (next, comparator_2_eq, comparator_2_lt);

  // Other names for the same wires on the sheet: clk = clock; paddress[8:1] = displayout

  // Notes on the sheet:
  //   clock: Hz: 500
  //   contents of ROMFILE (hex, n*v repeats v):
  //   0,0,c00,13*0,100,100,d00,13*0,200,200,c00,13*0,300,300,d00,13*0
  //   ,400,400,c00,13*0,500,500,d00,13*0,600,600,c00,13*0,700,700,d00
  //   ,13*0,800,800,c00,13*0,900,900,d00,13*0,a00,a00,c00,13*0,b00,b00,d00
endmodule

/* Test case FINALT1:
clock N reset start valid displayout done clockcount
            program(4,3,1,2)
0 4 0 0 X X X X
1 4 0 0 X X X X
0 4 1 0 X X X X
1 4 1 0 X X X X
0 4 0 1 X X X X
1 4 0 1 X X X X
repeat (40000) C 4 0 1 X X X X
1 4 0 1 X X X 0xBAADBEEF
*/

/* Test case FINALT2:
clock N reset start valid displayout done clockcount
            program(255,2,3,2)
0 4 0 0 X X X X
1 4 0 0 X X X X
0 4 1 0 X X X X
1 4 1 0 X X X X
0 4 0 1 X X X X
1 4 0 1 X X X X
repeat (40000) C 4 0 1 X X X X
1 4 0 1 X X X 0xBAADBEEF
*/

/* Test case FINALT3:
clock N reset start valid displayout done clockcount
            program(0,1,2,3,4,5,6,7,8,9,10,11,12,13,14,15,16,17,18,19,20,21,22,23,24,25,26,27,28,29,30,31,32,33,34,35,36,37,38,39,40,41,42,43,44,45,46,47,48,49,50,51,52,53,54,55,56,57,58,59,60,61,62,63,64,65,66,67,68,69,70,71,72,73,74,75,76,77,78,79,80,81,82,83,84,85,86,87,88,89,90,91,92,93,94,95,96,97,98,99,100,101,102,103,104,105,106,107,108,109,110,111,112,113,114,115,116,117,118,119,120,121,122,123,124,125,126,127,128,129,130,131,132,133,134,135,136,137,138,139,140,141,142,143,144,145,146,147,148,149,150,151,152,153,154,155,156,157,158,159,160,161,162,163,164,165,166,167,168,169,170,171,172,173,174,175,176,177,178,179,180,181,182,183,184,185,186,187,188,189,190,191,192,193,194,195,196,197,198,199,200,201,202,203,204,205,206,207,208,209,210,211,212,213,214,215,216,217,218,219,220,221,222,223,224,225,226,227,228,229,230,231,232,233,234,235,236,237,238,239,240,241,242,243,244,245,246,247,248,249,250,251,252,253,254,255)
0 256 0 0 X X X X
1 256 0 0 X X X X
0 256 1 0 X X X X
1 256 1 0 X X X X
0 256 0 1 X X X X
1 256 0 1 X X X X
repeat (40000) C 256 0 1 X X X X
1 256 0 1 X X X 0xBAADBEEF
*/

/* Test case FINALT4:
clock N reset start valid displayout done clockcount
            program(0,0,1,1,2,2,3,3,4,4,5,5,6,6,7,7,8,8,9,9,10,10,11,11,12,12,13,13,14,14,15,15,16,16,17,17,18,18,19,19,20,20,21,21,22,22,23,23,24,24,25,25,26,26,27,27,28,28,29,29,30,30,31,31,32,32,33,33,34,34,35,35,36,36,37,37,38,38,39,39,40,40,41,41,42,42,43,43,44,44,45,45,46,46,47,47,48,48,49,49,50,50,51,51,52,52,53,53,54,54,55,55,56,56,57,57,58,58,59,59,60,60,61,61,62,62,63,63,64,64,65,65,66,66,67,67,68,68,69,69,70,70,71,71,72,72,73,73,74,74,75,75,76,76,77,77,78,78,79,79,80,80,81,81,82,82,83,83,84,84,85,85,86,86,87,87,88,88,89,89,90,90,91,91,92,92,93,93,94,94,95,95,96,96,97,97,98,98,99,99,100,100,101,101,102,102,103,103,104,104,105,105,106,106,107,107,108,108,109,109,110,110,111,111,112,112,113,113,114,114,115,115,116,116,117,117,118,118,119,119,120,120,121,121,122,122,123,123,124,124,125,125,126,126,127,127,128,128,129,129,130,130,131,131,132,132,133,133,134,134,135,135,136,136,137,137,138,138,139,139,140,140,141,141,142,142,143,143,144,144,145,145,146,146,147,147,148,148,149,149,150,150,151,151,152,152,153,153,154,154,155,155,156,156,157,157,158,158,159,159,160,160,161,161,162,162,163,163,164,164,165,165,166,166,167,167,168,168,169,169,170,170,171,171,172,172,173,173,174,174,175,175,176,176,177,177,178,178,179,179,180,180,181,181,182,182,183,183,184,184,185,185,186,186,187,187,188,188,189,189,190,190,191,191,192,192,193,193,194,194,195,195,196,196,197,197,198,198,199,199,200,200,201,201,202,202,203,203,204,204,205,205,206,206,207,207,208,208,209,209,210,210,211,211,212,212,213,213,214,214,215,215,216,216,217,217,218,218,219,219,220,220,221,221,222,222,223,223,224,224,225,225,226,226,227,227,228,228,229,229,230,230,231,231,232,232,233,233,234,234,235,235,236,236,237,237,238,238,239,239,240,240,241,241,242,242,243,243,244,244,245,245,246,246,247,247,248,248,249,249,250,250,251,251,252,252,253,253,254,254,255)
0 511 0 0 X X X X
1 511 0 0 X X X X
0 511 1 0 X X X X
1 511 1 0 X X X X
0 511 0 1 X X X X
1 511 0 1 X X X X
repeat (40000) C 511 0 1 X X X X
1 511 0 1 X X X 0xBAADBEEF
*/

/* Test case FINALT5:
clock N reset start valid displayout done clockcount
            program(99,183,239,24,109,113,147,248,108,168,224,36,130,98,82,45,227,187,98,241,166,122,206,216,106,32,220,239,155,108,56,168,136,202,194,117,216,39,207,214,3,237,110,48,176,11,189,184,4,134,78,17,221,92,142,33,77,207,185,243,85,255,159)
0 63 0 0 X X X X
1 63 0 0 X X X X
0 63 1 0 X X X X
1 63 1 0 X X X X
0 63 0 1 X X X X
1 63 0 1 X X X X
repeat (40000) C 63 0 1 X X X X
1 63 0 1 X X X 0xBAADBEEF
*/

/* Test case FINALT6:
clock N reset start valid displayout done clockcount
            program(255,254,253,252,251,250,249,248,247,246,245,244,243,242,241,240,239,238,237,236,235,234,233,232,231,230,229,228,227,226,225,224,223,222,221,220,219,218,217,216,215,214,213,212,211,210,209,208,207,206,205,204,203,202,201,200,199,198,197,196,195,194,193)
0 63 0 0 X X X X
1 63 0 0 X X X X
0 63 1 0 X X X X
1 63 1 0 X X X X
0 63 0 1 X X X X
1 63 0 1 X X X X
repeat (40000) C 63 0 1 X X X X
1 63 0 1 X X X 0xBAADBEEF
*/
